# Fritzing sketch Robotics (saved by Fritzing 0.9.3b)
breadboards: 1

parts:
  RF1 = nRF8001 Bluetooth LE Breakout
  Part1 = Arduino Uno (Rev3)
  Part2 = Adafruit Motor/Stepper/Servo Shield [part_number="Adafruit #1438"]
  U1 = BATTERY-2 [package=battery-aa]
  S1 = SWITCH-MOMENTARY-2 [package=tactile-switch-1101ne]
  M1 = DC Motor
  M2 = DC Motor
  M3 = DC Motor

nets:
  N1: RF1.SCK, Part2.D13
  N2: RF1.MISO, Part2.D12
  N3: RF1.MOSI, Part2.D11
  N4: RF1.REQ, Part2.D10
  N5: RF1.RDY, Part2.D2
  N6: RF1.RST, Part2.D9
  GND: RF1.GND, Part1.GND, Part2.GND, U1.-1
  VIN: RF1.VIN, Part2.+5V
  N7: Part2.M2A, M1.pin_1
  N8: Part2.M2B, M1.pin_2
  N9: Part2.M3A, M3.pin_2
  N10: Part2.M3B, M3.pin_1
  N11: Part2.M4B, M2.pin_2
  N12: Part2.M4A, M2.pin_1
  N13: Part2.VMOTOR, S1.1
  N14: U1.+1, S1.2

notes:
  Back Drive
  Steering
  Front Drive

custom parts:
  nRF8001 Bluetooth LE Breakout: nRF8001 Breakout Board
  Adafruit Motor/Stepper/Servo Shield: The original Adafruit Motorshield kit is one of our most beloved kits, which is why we decided to make something even better. We have upgraded the shield kit to make the bestest, easiest way to drive DC and Stepper motors. This shield will make quick work of your next robotics project! We kept the ability to drive up to 4 DC motors or 2 stepper motors, but added many improvements: Instead of a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
